# Fritzing sketch Ada_Dollhouse_schematic (saved by Fritzing 0.9.3b)

parts:
  SparkFun_16_I/O_Expander_-_SX1509 = sx1509 breakout
  Living1 = LED - 3mm [color="White (4500K)" package="3 mm [THT]"]
  Kitch1 = LED - 3mm [color="White (4500K)" package="3 mm [THT]"]
  Living2 = LED - 3mm [color="White (4500K)" package="3 mm [THT]"]
  Master = LED - 3mm [color="White (4500K)" package="3 mm [THT]"]
  Bath = LED - 3mm [color="White (4500K)" package="3 mm [THT]"]
  Kids = LED - 3mm [color="White (4500K)" package="3 mm [THT]"]
  Doorbell = Square Pushbutton
  Kitch2 = LED - 3mm [color="White (4500K)" package="3 mm [THT]"]
  Porch = LED - 3mm [color="White (4500K)" package="3 mm [THT]"]
  R1 = Resistor [tolerance=±5% resistance=220 package=THT]
  SP1 = SPEAKER [package=pcb_mount_speaker]
  PB-Living = Square Pushbutton
  PL-Living = smd LED [color="Green (570nm)" package="1206 [SMD]"]
  PB-Kitch = Square Pushbutton
  PL-Kitch = smd LED [color="White (8000K)" package="1206 [SMD]"]
  PB-Porch = Square Pushbutton
  PL-Porch = smd LED [color="Blue (430nm)" package="1206 [SMD]"]
  PB-Master = Square Pushbutton
  PL-Master = smd LED [color="Red (633nm)" package="1206 [SMD]"]
  PB-Bath = Square Pushbutton
  PL-Bath = smd LED [color="Orange (612nm)" package="1206 [SMD]"]
  PB-Kids = Square Pushbutton
  PL-Kids = smd LED [color="White (8000K)" package="1206 [SMD]"]
  Power = Square Pushbutton
  R2 = Resistor [tolerance=±5% resistance=220 package=THT]
  R3 = Resistor [tolerance=±5% resistance=220 package=THT]
  R4 = Resistor [tolerance=±5% resistance=220 package=THT]
  R5 = Resistor [tolerance=±5% resistance=220 package=THT]
  R6 = Resistor [tolerance=±5% resistance=220 package=THT]
  PL-Power = smd LED [color="Red (633nm)" package="1206 [SMD]"]
  R7 = Resistor [tolerance=±5% resistance=220 package=THT]
  TLC5947 = 24-Channel 12-bit PWM LED Driver - SPI [part_number=1429]
  Sparkfun_Pro_Micro_3_3V = SparkFun Pro Micro
  Adafruit_Audio_FX_Mini_Sound_Board = Adafruit Audio FX Mini Sound Board [part_number="Adafruit #2342 and #2220"]
  SparkFun_Mono_Audio_Amp_Breakout = Mono Audio Amp Breakout
  R8 = Resistor [tolerance=±5% resistance=100k package=THT]
  R9 = Resistor [tolerance=±5% resistance=220 package=THT]
  Part2 = PowerBoost 500 Charger
  J1 = USB Connectors [package=usb-a-h]
  B1 = LIPO-2000mAh [part_number=4400mAh package=lipo-2000]
  R10 = Resistor [tolerance=±5% resistance=100k package=THT]
  Q1 = MOSFET-NCHANNEL [package=to-92]
  J2 = USB_MICROB_PLUG [package=micro-b-ra-smt]
  Part3 = Adafruit Push Button Powerswitch (modified [part_number="Adafruit #1400"]

nets:
  IOB-INTn: SparkFun_16_I/O_Expander_-_SX1509.!INT, Sparkfun_Pro_Micro_3_3V.7
  IOB-SCL: SparkFun_16_I/O_Expander_-_SX1509.SCL, Sparkfun_Pro_Micro_3_3V.3
  GND: SparkFun_16_I/O_Expander_-_SX1509.GND, Doorbell.leg0, PB-Living.leg0, PB-Kitch.leg0, PB-Porch.leg0, PB-Master.leg0, PB-Bath.leg0, PB-Kids.leg0, TLC5947.GND, Sparkfun_Pro_Micro_3_3V.GND, Adafruit_Audio_FX_Mini_Sound_Board.GND, Adafruit_Audio_FX_Mini_Sound_Board.UG, SparkFun_Mono_Audio_Amp_Breakout.IN-, SparkFun_Mono_Audio_Amp_Breakout.GND, R8.Pin_1, Part2.GND, J1.GND, B1.-, Q1.S, J2.GND, Part3.GND
  3.3V: SparkFun_16_I/O_Expander_-_SX1509.3.3V, R1.Pin_1, R2.Pin_1, R3.Pin_1, R4.Pin_1, R5.Pin_1, R6.Pin_1, R7.Pin_1, Sparkfun_Pro_Micro_3_3V.VCC, R9.Pin_1, R10.Pin_0
  IOB-SDA: SparkFun_16_I/O_Expander_-_SX1509.SDA, Sparkfun_Pro_Micro_3_3V.2
  N1: SparkFun_16_I/O_Expander_-_SX1509.0, PB-Living.leg1
  N2: SparkFun_16_I/O_Expander_-_SX1509.1, PB-Kitch.leg1
  N3: SparkFun_16_I/O_Expander_-_SX1509.2, PB-Porch.leg1
  N4: SparkFun_16_I/O_Expander_-_SX1509.3, PB-Master.leg1
  N5: SparkFun_16_I/O_Expander_-_SX1509.4, PL-Living.cathode
  N6: SparkFun_16_I/O_Expander_-_SX1509.5, PL-Kitch.cathode
  N7: SparkFun_16_I/O_Expander_-_SX1509.6, PL-Porch.cathode
  N8: SparkFun_16_I/O_Expander_-_SX1509.7, PL-Master.cathode
  N9: SparkFun_16_I/O_Expander_-_SX1509.8, PB-Bath.leg1
  N10: SparkFun_16_I/O_Expander_-_SX1509.9, PB-Kids.leg1
  N11: SparkFun_16_I/O_Expander_-_SX1509.10, Doorbell.leg1
  N/C: SparkFun_16_I/O_Expander_-_SX1509.11, TLC5947.PWM5
  N12: SparkFun_16_I/O_Expander_-_SX1509.12, PL-Bath.cathode
  N13: SparkFun_16_I/O_Expander_-_SX1509.13, PL-Kids.cathode
  N14: SparkFun_16_I/O_Expander_-_SX1509.14, PL-Power.cathode
  N15: Living1.cathode, TLC5947.PWM0
  5V: Living1.anode, Kitch1.anode, Living2.anode, Master.anode, Bath.anode, Kids.anode, Kitch2.anode, Porch.anode, TLC5947.+24V, Sparkfun_Pro_Micro_3_3V.RAW, Adafruit_Audio_FX_Mini_Sound_Board.VIN, SparkFun_Mono_Audio_Amp_Breakout.VIN
  N16: Kitch1.cathode, TLC5947.PWM2
  N17: Living2.cathode, TLC5947.PWM1
  N18: Master.cathode, TLC5947.PWM6
  N19: Bath.cathode, TLC5947.PWM7
  N20: Kids.cathode, TLC5947.PWM8
  N21: Kitch2.cathode, TLC5947.PWM3
  N22: Porch.cathode, TLC5947.PWM4
  N23: R1.Pin_0, PL-Living.anode
  N24: SP1.+, SparkFun_Mono_Audio_Amp_Breakout.OUT+
  N25: SP1.-, SparkFun_Mono_Audio_Amp_Breakout.OUT-
  N26: PL-Kitch.anode, R2.Pin_0
  N27: PL-Porch.anode, R3.Pin_0
  N28: PL-Master.anode, R4.Pin_0
  N29: PL-Bath.anode, R5.Pin_0
  N30: PL-Kids.anode, R6.Pin_0
  PWR-SW-2: Power.leg0
  PWR-SW-1: Power.leg1
  N31: PL-Power.anode, R7.Pin_0
  PWM-LAT: TLC5947.LAT, Sparkfun_Pro_Micro_3_3V.14
  PWM-BLANK: TLC5947.OE, Sparkfun_Pro_Micro_3_3V.8, R9.Pin_0
  PWM-CLK: TLC5947.CLK, Sparkfun_Pro_Micro_3_3V.15
  PWM-DIN: TLC5947.DIN, Sparkfun_Pro_Micro_3_3V.16
  SND-RXin: Sparkfun_Pro_Micro_3_3V.TX0, Adafruit_Audio_FX_Mini_Sound_Board.RX_5V
  SND-TXout: Sparkfun_Pro_Micro_3_3V.RX1, Adafruit_Audio_FX_Mini_Sound_Board.TX
  AMP-SDNn: Sparkfun_Pro_Micro_3_3V.4, SparkFun_Mono_Audio_Amp_Breakout.S, R8.Pin_0
  SFX-RST: Sparkfun_Pro_Micro_3_3V.5, Adafruit_Audio_FX_Mini_Sound_Board.RST
  PWR-OFF: Sparkfun_Pro_Micro_3_3V.6, Part3.OFF
  BAT-LOW: Sparkfun_Pro_Micro_3_3V.9, R10.Pin_1, Q1.D
  N32: Adafruit_Audio_FX_Mini_Sound_Board.L_AC, SparkFun_Mono_Audio_Amp_Breakout.IN+
  N33: Part2.VBAT, B1.+, Part3.IN
  N34: Part2.ENABLE, Part3.GATE
  N35: Part2.LBO, Q1.G
  N36: Part2.USB, J1.D+
  N37: Part2.5.0V, J2.VCC
  N38: J1.D-, J2.D-
  N39: J1.VBUS, J2.D+

notes:
  Living Room
  Doorbell
  Kitchen
  Porch
  Master
  Bathroom
  Kids
  Main Power
  All Off
  Ada's Dollhouse Conroller, 4
  Main Power Input
  blk
  red
  GATE

custom parts:
  24-Channel 12-bit PWM LED Driver - SPI: This breakout board for the TLC5947 PWM driver chip can control 24 separate channels of 12-bit PWM output. Designed (and ideal) for LED control, this board is NOT good for driving servos. Only three "SPI" pins are required to send data (our Arduino library shows how to to use any digital microcontroller pins). Best of all, the design is completely chainable. As long as there's enough power for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
  SparkFun Pro Micro: The Pro Micro is similar to the Pro Mini except with an ATmega32U4 on board. The USB transceiver inside the 32U4 allows us to add USB connectivity on-board and do away with bulky external USB interface. Based on: https://github.com/unorthodox-engineers/unorthodox-arduino/blob/master/Unorthodox/fritzing/parts/Pro%20Micro.fzpz
  Adafruit Audio FX Mini Sound Board: Would you like to add audio/sound effects to your next project, without an Arduino+Shield? Or maybe you don't even know how to use microcontrollers, you just want to make a sound play whenever you press a button. What about something that has to be very small and portable? You are probably feeling a little frustrated: it's been very hard to find a simple, low cost audio effects trigger that is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
  Mono Audio Amp Breakout: Description: This tiny audio amplifier is based on the Texas Instruments TPA2005D1. Its efficient class-D operation means low heat and long battery life. It can drive an 8-Ohm speaker at up to 1.4 Watts; it won't shake a stadium, but it will provide plenty of volume for your audio projects. The fully-differential inputs are safe for floating audio signals such as from our MP3 Shield, and can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
  PowerBoost 500 Charger: The PowerBoost 500C is a little DC/DC boost converter module that can be powered by any 3.7V LiIon/LiPoly battery, and convert the battery output to 5.2V DC for running your 5V projects. At its heart is a TPS61090 boost converter from TI. This boost converter chip has some really nice extras such as low battery detection, 2A internal switch, synchronous conversion, excellent efficiency, and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
  Adafruit Push Button Powerswitch (modified: **Modified to provide the GATE signal as a direct output (power FET not used)** The Adafruit Push-button Power Switch is a tidy little design that lets you control a DC power source using an everyday tactile button. The breakout uses a latching analog circuit that is triggered by a push of the button. Press once to turn on, then press again to turn off. The circuit uses a 3A P-FET to connect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
